// Logisim project MAFF LINDA.circ as structural Verilog: 4 circuits, main circuit main
module main (
  input  A,
  input  B,
  input  C,
  input  D,
  output F
);

  wire and_1_out, and_2_out, and_3_out, and_4_out, not_1_out, not_2_out, or_1_out;

  not not_1 (not_1_out, B);
  not not_2 (not_2_out, B);
  and and_1 (and_1_out, A, not_1_out);
  and and_2 (and_2_out, not_2_out, C);
  buf and_3 (and_3_out, A);  // AND_Gate
  or or_1 (or_1_out, and_2_out, and_3_out);
  and and_4 (and_4_out, and_1_out, or_1_out);
  or or_2 (F, and_4_out, C);
endmodule

module MAFF_LINDA_1_1 (
  input  A,
  input  B,
  input  C,
  input  D,
  output F
);

  wire and_1_out, and_2_out, not_1_out, not_2_out, or_1_out;

  not not_1 (not_1_out, B);
  and and_1 (and_1_out, not_1_out, C);
  not not_2 (not_2_out, B);
  or or_1 (or_1_out, and_1_out, A);
  and and_2 (and_2_out, A, not_2_out, or_1_out);
  or or_2 (F, and_2_out, C);
endmodule

module MAFF_LINDA_1_2 (
  input  A,
  input  B,
  input  C,
  output F
);

  wire and_1_out, and_2_out, and_3_out, and_4_out, not_1_out, not_2_out, not_3_out, or_1_out;

  not not_1 (not_1_out, A);
  not not_2 (not_2_out, B);
  not not_3 (not_3_out, C);
  and and_1 (and_1_out, not_1_out, not_2_out, not_3_out);
  and and_2 (and_2_out, A, B);
  and and_3 (and_3_out, A, C);
  and and_4 (and_4_out, B, C);
  or or_1 (or_1_out, and_1_out, and_2_out, and_3_out);
  or or_2 (F, or_1_out, and_4_out);
endmodule

module MAFF_LINDA_1_4 (
  input  A,
  input  B,
  input  C
);

  wire not_1_out, not_2_out, not_3_out;

  not not_1 (not_1_out, A);
  not not_2 (not_2_out, B);
  not not_3 (not_3_out, C);
  // NAND_Gate nand_1 has open pins: in0=not_1_out, in1=not_2_out, in2=not_3_out, out=open
endmodule
