// Logisim project MAFF LINDA1.1.circ as structural Verilog: 2 circuits, main circuit main
module main (
  input  A,
  input  B,
  input  C,
  input  D,
  output F
);

  wire and_1_out, and_2_out, and_3_out, and_4_out, not_1_out, not_2_out, or_1_out;

  not not_1 (not_1_out, B);
  not not_2 (not_2_out, B);
  and and_1 (and_1_out, A, not_1_out);
  and and_2 (and_2_out, not_2_out, C);
  buf and_3 (and_3_out, A);  // AND_Gate
  or or_1 (or_1_out, and_2_out, and_3_out);
  and and_4 (and_4_out, and_1_out, or_1_out);
  or or_2 (F, and_4_out, C);
endmodule

module MAFF_LINDA_1_1 (
  input  A,
  input  B,
  input  C,
  input  D,
  output F
);

  wire and_1_out, and_2_out, not_1_out, not_2_out, or_1_out;

  not not_1 (not_1_out, B);
  and and_1 (and_1_out, not_1_out, C);
  not not_2 (not_2_out, B);
  or or_1 (or_1_out, and_1_out, A);
  and and_2 (and_2_out, A, not_2_out, or_1_out);
  or or_2 (F, and_2_out, C);
endmodule
