// Logisim project Modo Oscilação.circ as structural Verilog: 1 circuit, main circuit main
module main (
  input  BO,
  input  BLD
);

  wire and_1_out, and_2_out, and_3_out, and_4_out, and_5_out, and_6_out, and_7_out, and_8_out, and_9_out,
       and_10_out, clock_1_out, not_1_out, not_2_out, not_3_out, not_4_out, or_1_out, or_2_out, or_3_out,
       T1_q, T2_q, T3_q;

  Clock clock_1 (.out(clock_1_out));
  and and_1 (and_1_out, not_1_out, not_3_out, BLD, BO);
  not not_1 (not_1_out, T1_q);
  not not_2 (not_2_out, T3_q);
  not not_3 (not_3_out, T2_q);
  and and_2 (and_2_out, BLD, not_2_out, not_3_out, not_1_out);
  and and_3 (and_3_out, not_2_out, BO, BLD);
  or or_1 (or_1_out, and_1_out, and_2_out, and_3_out, and_4_out, and_5_out);
  and and_4 (and_4_out, T1_q, not_3_out, BLD);
  and and_5 (and_5_out, T1_q, not_2_out, BLD);
  T_Flip_Flop T1 (.clk(clock_1_out), .T(or_1_out), .Q(T1_q));  // open: Qn, preset, reset, en
  not not_4 (not_4_out, BLD);
  and and_6 (and_6_out, not_4_out, not_3_out);
  and and_7 (and_7_out, BLD, BO, not_2_out, T1_q);
  or or_2 (or_2_out, and_7_out, and_6_out);
  T_Flip_Flop T2 (.clk(clock_1_out), .T(or_2_out), .Q(T2_q));  // open: Qn, preset, reset, en
  and and_8 (and_8_out, BLD, BO, not_2_out, T1_q, T2_q);
  and and_9 (and_9_out, not_4_out, T3_q);
  or or_3 (or_3_out, and_8_out, and_9_out, and_10_out);
  and and_10 (and_10_out, BO, T3_q, T1_q);
  T_Flip_Flop T3 (.clk(clock_1_out), .T(or_3_out), .Q(T3_q));  // open: Qn, preset, reset, en
  LED MO (.in(BO));
  LED SD (.in(T2_q));
  LED SE (.in(T3_q));
endmodule
