// Logisim project Modo funcionamento.circ as structural Verilog: 1 circuit, main circuit main
module main (
  input  in_1
);

  wire and_1_out, and_2_out, and_3_out, and_4_out, and_5_out, and_6_out, and_7_out, button_1_out,
       clock_1_out, not_1_out, not_2_out, not_3_out, not_4_out, or_1_out, or_2_out, or_3_out, T1_q, T2_q,
       xor_1_out;

  Button button_1 (.out(button_1_out));
  Clock clock_1 (.out(clock_1_out));
  and and_1 (and_1_out, button_1_out, in_1, not_1_out);
  not not_1 (not_1_out, T1_q);
  and and_2 (and_2_out, not_1_out, not_3_out, in_1);
  or or_1 (or_1_out, and_1_out, and_2_out, and_3_out, and_4_out);
  not not_2 (not_2_out, in_1);
  not not_3 (not_3_out, T2_q);
  and and_3 (and_3_out, not_3_out, T1_q, button_1_out);
  and and_4 (and_4_out, not_2_out, T1_q);
  and and_5 (and_5_out, in_1, button_1_out, T1_q);
  and and_6 (and_6_out, T2_q, not_2_out);
  or or_2 (or_2_out, and_6_out, and_5_out);
  T_Flip_Flop T1 (.clk(clock_1_out), .T(or_1_out), .Q(T1_q));  // open: Qn, preset, reset, en
  T_Flip_Flop T2 (.clk(clock_1_out), .T(or_2_out), .Q(T2_q));  // open: Qn, preset, reset, en
  not not_4 (not_4_out, T1_q);
  xor xor_1 (xor_1_out, T2_q, T1_q);
  and and_7 (and_7_out, not_4_out, T2_q);
  or or_3 (or_3_out, T1_q, T2_q);
  LED R1 (.in(xor_1_out));
  LED R2 (.in(and_7_out));
  LED MV (.in(or_3_out));
endmodule
