// Logisim project Termoventilador.circ as structural Verilog: 1 circuit, main circuit main
module main (
  input  BLD,
  input  BO
);

  wire and_1_out, and_2_out, and_3_out, and_4_out, and_5_out, and_6_out, and_7_out, and_8_out, and_9_out,
       and_10_out, and_11_out, and_12_out, and_13_out, and_14_out, and_15_out, and_16_out, and_17_out,
       BM_out, clock_1_out, not_1_out, not_2_out, not_3_out, not_4_out, not_5_out, not_6_out, not_7_out,
       not_8_out, or_1_out, or_2_out, or_3_out, or_4_out, or_5_out, or_6_out, T1_2_q, T1_q, T2_2_q, T2_q,
       T3_q, xor_1_out;

  Button BM (.out(BM_out));
  Clock clock_1 (.out(clock_1_out));
  not not_1 (not_1_out, T1_q);
  and and_1 (and_1_out, BM_out, BLD, not_1_out);
  not not_2 (not_2_out, T2_q);
  and and_2 (and_2_out, not_1_out, not_2_out, BLD);
  and and_3 (and_3_out, not_2_out, T1_q, BM_out);
  or or_1 (or_1_out, and_1_out, and_2_out, and_3_out, and_6_out);
  not not_3 (not_3_out, T3_q);
  not not_4 (not_4_out, T1_2_q);
  not not_5 (not_5_out, T2_2_q);
  and and_4 (and_4_out, BLD, not_3_out, not_5_out, not_4_out);
  and and_5 (and_5_out, not_4_out, not_5_out, BLD, BO);
  not not_6 (not_6_out, BLD);
  and and_6 (and_6_out, not_6_out, T1_q);
  and and_7 (and_7_out, T1_2_q, not_5_out, BLD);
  and and_8 (and_8_out, not_3_out, BO, BLD);
  or or_2 (or_2_out, and_5_out, and_4_out, and_8_out, and_7_out, and_10_out);
  and and_9 (and_9_out, T2_q, not_6_out);
  or or_3 (or_3_out, and_9_out, and_11_out);
  and and_10 (and_10_out, T1_2_q, not_3_out, BLD);
  T_Flip_Flop T1 (.clk(clock_1_out), .T(or_1_out), .Q(T1_q));  // open: Qn, preset, reset, en
  and and_11 (and_11_out, BLD, BM_out, T1_q);
  and and_12 (and_12_out, BLD, BO, not_3_out, T1_2_q);
  or or_4 (or_4_out, and_12_out, and_13_out);
  T_Flip_Flop T1_2 (.clk(clock_1_out), .T(or_2_out), .Q(T1_2_q));  // open: Qn, preset, reset, en
  not not_7 (not_7_out, BLD);
  and and_13 (and_13_out, not_7_out, not_5_out);
  T_Flip_Flop T2 (.clk(clock_1_out), .T(or_3_out), .Q(T2_q));  // open: Qn, preset, reset, en
  T_Flip_Flop T2_2 (.clk(clock_1_out), .T(or_4_out), .Q(T2_2_q));  // open: Qn, preset, reset, en
  and and_14 (and_14_out, not_7_out, T3_q);
  and and_15 (and_15_out, BLD, BO, not_3_out, T1_2_q, T2_2_q);
  or or_5 (or_5_out, and_15_out, and_14_out, and_16_out);
  and and_16 (and_16_out, BO, T3_q, T1_2_q);
  not not_8 (not_8_out, T1_q);
  or or_6 (or_6_out, T1_q, T2_q);
  xor xor_1 (xor_1_out, T2_q, T1_q);
  and and_17 (and_17_out, not_8_out, T2_q);
  T_Flip_Flop T3 (.clk(clock_1_out), .T(or_5_out), .Q(T3_q));  // open: Qn, preset, reset, en
  LED R1 (.in(xor_1_out));
  LED R2 (.in(and_17_out));
  LED MV (.in(or_6_out));
  LED MO (.in(BO));
  LED SD (.in(T2_2_q));
  LED SE (.in(T3_q));
endmodule
